// Logisim project 7400-series.circ as structural Verilog
module _74HC595 (
  input  SRCLR__ACTIVELOW,
  input  SER,
  input  RCLK,
  input  SRCLK,
  input  OE__ACTIVELOW,
  input  Vcc,
  input  GND,
  output QH_prime,
  output QA,
  output QC,
  output QD,
  output QE,
  output QF,
  output QG,
  output QB,
  output QH
);

  wire and_1_out, d_ff_1_q, d_ff_2_q, d_ff_3_q, d_ff_4_q, d_ff_5_q, d_ff_6_q, d_ff_7_q, d_ff_8_q, d_ff_9_q,
       d_ff_10_q, d_ff_11_q, d_ff_12_q, d_ff_13_q, d_ff_14_q, d_ff_16_q, not_1_out, not_2_out, not_3_out;

  not not_1 (not_1_out, SRCLR__ACTIVELOW);
  not not_2 (not_2_out, OE__ACTIVELOW);
  D_Flip_Flop d_ff_1 (.clk(SRCLK), .D(SER), .Q(d_ff_1_q), .reset(not_1_out));  // open: Qn, preset, en
  D_Flip_Flop d_ff_2 (.clk(RCLK), .D(d_ff_1_q), .Q(d_ff_2_q));  // open: Qn, preset, en, reset
  assign QA = not_2_out ? d_ff_2_q : 1'bz;  // Controlled_Buffer controlled_buffer_1
  not not_3 (not_3_out, GND);
  D_Flip_Flop d_ff_3 (.clk(RCLK), .D(d_ff_4_q), .Q(d_ff_3_q));  // open: Qn, preset, en, reset
  assign QB = not_2_out ? d_ff_3_q : 1'bz;  // Controlled_Buffer controlled_buffer_2
  and and_1 (and_1_out, Vcc, not_3_out);
  D_Flip_Flop d_ff_4 (.clk(SRCLK), .D(d_ff_1_q), .Q(d_ff_4_q), .reset(not_1_out));  // open: Qn, preset, en
  D_Flip_Flop d_ff_5 (.clk(SRCLK), .D(d_ff_4_q), .Q(d_ff_5_q), .reset(not_1_out));  // open: Qn, preset, en
  D_Flip_Flop d_ff_6 (.clk(RCLK), .D(d_ff_5_q), .Q(d_ff_6_q));  // open: Qn, preset, en, reset
  assign QC = not_2_out ? d_ff_6_q : 1'bz;  // Controlled_Buffer controlled_buffer_3
  D_Flip_Flop d_ff_7 (.clk(SRCLK), .D(d_ff_5_q), .Q(d_ff_7_q), .reset(not_1_out));  // open: Qn, preset, en
  D_Flip_Flop d_ff_8 (.clk(RCLK), .D(d_ff_7_q), .Q(d_ff_8_q));  // open: Qn, preset, en, reset
  assign QD = not_2_out ? d_ff_8_q : 1'bz;  // Controlled_Buffer controlled_buffer_4
  D_Flip_Flop d_ff_9 (.clk(SRCLK), .D(d_ff_7_q), .Q(d_ff_9_q), .reset(not_1_out));  // open: Qn, preset, en
  D_Flip_Flop d_ff_10 (.clk(RCLK), .D(d_ff_9_q), .Q(d_ff_10_q));  // open: Qn, preset, en, reset
  assign QE = not_2_out ? d_ff_10_q : 1'bz;  // Controlled_Buffer controlled_buffer_5
  D_Flip_Flop d_ff_11 (.clk(SRCLK), .D(d_ff_9_q), .Q(d_ff_11_q), .reset(not_1_out));  // open: Qn, preset, en
  D_Flip_Flop d_ff_12 (.clk(RCLK), .D(d_ff_11_q), .Q(d_ff_12_q));  // open: Qn, preset, en, reset
  assign QF = not_2_out ? d_ff_12_q : 1'bz;  // Controlled_Buffer controlled_buffer_6
  D_Flip_Flop d_ff_13 (.clk(SRCLK), .D(d_ff_11_q), .Q(d_ff_13_q), .reset(not_1_out));  // open: Qn, preset, en
  D_Flip_Flop d_ff_14 (.clk(RCLK), .D(d_ff_13_q), .Q(d_ff_14_q));  // open: Qn, preset, en, reset
  assign QG = not_2_out ? d_ff_14_q : 1'bz;  // Controlled_Buffer controlled_buffer_7
  D_Flip_Flop d_ff_15 (.clk(SRCLK), .D(d_ff_13_q), .Q(QH_prime), .reset(not_1_out));  // open: Qn, preset, en
  D_Flip_Flop d_ff_16 (.clk(RCLK), .D(QH_prime), .Q(d_ff_16_q));  // open: Qn, preset, en, reset
  assign QH = not_2_out ? d_ff_16_q : 1'bz;  // Controlled_Buffer controlled_buffer_8
endmodule

module _74xx23 (
  input  _1A,
  input  _1B,
  input  _1C,
  input  _1D,
  input  _1G,
  input  _2A,
  input  _2B,
  input  _2C,
  input  _2D,
  input  _2G,
  input  Vcc,
  input  GND,
  output _1Y,
  output _2Y
);

  wire and_1_out, and_2_out, and_3_out, and_4_out, and_5_out, and_6_out, and_7_out, and_8_out, or_1_out,
       or_2_out;

  and and_1 (and_1_out, _1A, _1G);
  and and_2 (and_2_out, _1B, _1G);
  and and_3 (and_3_out, _1C, _1G);
  and and_4 (and_4_out, _1G, _1D);
  and and_5 (and_5_out, _2A, _2G);
  and and_6 (and_6_out, _2B, _2G);
  and and_7 (and_7_out, _2C, _2G);
  and and_8 (and_8_out, _2G, _2D);
  or or_1 (or_1_out, and_1_out, and_2_out, and_3_out, and_4_out);
  or or_2 (or_2_out, and_5_out, and_6_out, and_7_out, and_8_out);
  not not_1 (_1Y, or_1_out);
  not not_2 (_2Y, or_2_out);
endmodule

module _74xx36 (
  input  _1A,
  input  _1B,
  input  _2A,
  input  _2B,
  input  _3A,
  input  _3B,
  input  _4A,
  input  _4B,
  input  Vcc,
  input  GND,
  output _1Y,
  output _2Y,
  output _3Y,
  output _4Y
);

  nor nor_1 (_1Y, _1A, _1B);
  nor nor_2 (_2Y, _2A, _2B);
  nor nor_3 (_3Y, _3A, _3B);
  nor nor_4 (_4Y, _4A, _4B);
endmodule

module _74xx43 (
  input  A,
  input  B,
  input  C,
  input  D,
  input  Vcc,
  input  GND,
  output _0,
  output _1,
  output _2,
  output _3,
  output _4,
  output _5,
  output _6,
  output _7,
  output _8,
  output _9
);

  wire not_1_out, not_2_out, not_3_out, not_4_out, not_5_out, not_6_out, not_7_out, not_8_out;

  not not_1 (not_1_out, A);
  not not_2 (not_2_out, C);
  not not_3 (not_3_out, D);
  not not_4 (not_4_out, not_3_out);
  not not_5 (not_5_out, not_1_out);
  not not_6 (not_6_out, B);
  not not_7 (not_7_out, not_6_out);
  not not_8 (not_8_out, not_2_out);
  nand nand_1 (_1, not_8_out, not_1_out, not_6_out, not_3_out);
  nand nand_2 (_2, not_6_out, not_3_out, not_5_out, not_8_out, not_8_out);
  nand nand_3 (_3, not_1_out, not_7_out, not_8_out, not_3_out);
  nand nand_4 (_4, not_5_out, not_7_out, not_3_out, not_8_out);
  nand nand_5 (_5, not_1_out, not_6_out, not_2_out, not_4_out);
  nand nand_6 (_0, not_5_out, not_7_out, not_2_out, not_3_out);
  nand nand_7 (_6, not_6_out, not_2_out, not_5_out, not_4_out);
  nand nand_8 (_7, not_7_out, not_1_out, not_2_out, not_4_out);
  nand nand_9 (_8, not_2_out, not_5_out, not_7_out, not_4_out);
  nand nand_10 (_9, not_1_out, not_6_out, not_8_out, not_4_out);

  // Notes on the sheet:
  //   SUBTRACT 3 FROM XS3 REP TO GET REAL VALUE
  //   ADD 3 TO REAL VALUE TO GET XS3
endmodule

module _74xx53 (
  input  X,
  input  A,
  input  B,
  input  C,
  input  D,
  input  E,
  input  F,
  input  G,
  input  H,
  input  Vcc,
  input  GND,
  output Y,
  output Xnot
);

  wire and_1_out, and_2_out, and_3_out, and_4_out, or_1_out;

  and and_1 (and_1_out, A, B);
  and and_2 (and_2_out, C, D);
  and and_3 (and_3_out, E, F);
  and and_4 (and_4_out, G, H);
  or or_1 (or_1_out, and_1_out, and_2_out, X, and_3_out, and_4_out);
  not not_1 (Y, or_1_out);
  not not_2 (Xnot, X);
endmodule

module _74xx60 (
  input  _1A,
  input  _1B,
  input  _1C,
  input  _1D,
  input  _2A,
  input  _2B,
  input  _2C,
  input  _2D,
  input  Vcc,
  input  GND,
  output _1Xnot,
  output _1X,
  output _2Xnot,
  output _2X
);

  and and_1 (_1X, _1A, _1B, _1C, _1D);
  and and_2 (_2X, _2A, _2B, _2C, _2D);
  not not_1 (_1Xnot, _1X);
  not not_2 (_2Xnot, _2X);
endmodule

module _74xx85 (
  input  A3,
  input  A2,
  input  A1,
  input  A0,
  input  B3,
  input  B2,
  input  B1,
  input  B0,
  input  A_Bin,
  input  A_Bin_2,
  input  A_Bin_3,
  input  Vcc,
  input  GND,
  output A_Bout,
  output A_Bout_2,
  output A_Bout_3
);

  wire and_1_out, and_2_out, and_3_out, and_4_out, and_5_out, and_6_out, and_7_out, and_8_out, and_9_out,
       and_10_out, nor_1_out, nor_2_out, nor_3_out, not_1_out, not_2_out, not_3_out, not_4_out, not_5_out,
       not_6_out, not_7_out, not_8_out, not_9_out, not_10_out, not_11_out, not_12_out, not_13_out,
       not_14_out, xor_1_out, xor_2_out, xor_3_out, xor_4_out;

  and and_1 (and_1_out, A3, not_1_out);
  not not_1 (not_1_out, B3);
  not not_2 (not_2_out, B0);
  not not_3 (not_3_out, A0);
  not not_4 (not_4_out, xor_1_out);
  xor xor_1 (xor_1_out, A3, B3);
  not not_5 (not_5_out, B2);
  xor xor_2 (xor_2_out, A2, B2);
  xor xor_3 (xor_3_out, A0, B0);
  not not_6 (not_6_out, A3);
  and and_2 (and_2_out, B3, not_6_out);
  not not_7 (not_7_out, A2);
  and and_3 (and_3_out, not_7_out, not_4_out, B2);
  and and_4 (and_4_out, B1, nor_1_out, not_8_out);
  not not_8 (not_8_out, A1);
  and and_5 (and_5_out, nor_2_out, B0, not_3_out);
  not not_9 (not_9_out, A_Bin);
  and and_6 (and_6_out, not_9_out, nor_3_out, not_10_out);
  not not_10 (not_10_out, A_Bin_3);
  and and_7 (and_7_out, not_4_out, A2, not_5_out);
  nor nor_1 (nor_1_out, xor_1_out, xor_2_out);
  not not_11 (not_11_out, B1);
  xor xor_4 (xor_4_out, A1, B1);
  and and_8 (and_8_out, nor_1_out, A1, not_11_out);
  nor nor_2 (nor_2_out, xor_1_out, xor_2_out, xor_4_out);
  and and_9 (and_9_out, nor_2_out, A0, not_2_out);
  not not_12 (not_12_out, nor_2_out);
  nor nor_3 (nor_3_out, not_12_out, xor_3_out);
  not not_13 (not_13_out, A_Bin_2);
  not not_14 (not_14_out, A_Bin_3);
  and and_10 (and_10_out, nor_3_out, not_13_out, not_14_out);
  or or_1 (A_Bout_2, and_2_out, and_3_out, and_6_out, and_4_out, and_5_out);
  or or_2 (A_Bout, and_1_out, and_7_out, and_8_out, and_9_out, and_10_out);
  and and_11 (A_Bout_3, nor_3_out, A_Bin_3);

  // Notes on the sheet:
  //   EQUAL
endmodule

module _74xx99 (
  input  A,
  input  B,
  input  C,
  input  D,
  input  MODE,
  input  J,
  input  KNOT,
  input  CLK1,
  input  CLK2,
  input  Vcc,
  input  GND,
  output QA,
  output QB,
  output QC,
  output QD,
  output QDNOT
);

  wire and_1_out, and_2_out, and_3_out, and_4_out, and_5_out, d_ff_1_qn, multiplexer_1_out,
       multiplexer_2_out, multiplexer_3_out, multiplexer_4_out, not_1_out, not_2_out, not_3_out, not_4_out,
       or_1_out, or_2_out;

  not not_1 (not_1_out, KNOT);
  not not_2 (not_2_out, MODE);
  and and_1 (and_1_out, J, KNOT);
  and and_2 (and_2_out, d_ff_1_qn, J, not_1_out);
  not not_3 (not_3_out, J);
  and and_3 (and_3_out, not_3_out, KNOT, QA);
  and and_4 (and_4_out, not_2_out, CLK1);
  and and_5 (and_5_out, MODE, CLK2);
  Multiplexer #(.enable("false")) multiplexer_1 (.in0(or_1_out), .in1(A), .out(multiplexer_1_out), .sel(MODE));
  or or_1 (or_1_out, and_1_out, and_2_out, and_3_out);
  or or_2 (or_2_out, and_4_out, and_5_out);
  not not_4 (not_4_out, or_2_out);
  Multiplexer #(.enable("false")) multiplexer_2 (.in0(QA), .in1(B), .out(multiplexer_2_out), .sel(MODE));
  Multiplexer #(.enable("false")) multiplexer_3 (.in0(QB), .in1(C), .out(multiplexer_3_out), .sel(MODE));
  Multiplexer #(.enable("false")) multiplexer_4 (.in0(QC), .in1(D), .out(multiplexer_4_out), .sel(MODE));
  D_Flip_Flop d_ff_1 (.clk(not_4_out), .D(multiplexer_1_out), .Q(QA), .Qn(d_ff_1_qn));  // open: preset, en, reset
  D_Flip_Flop d_ff_2 (.clk(not_4_out), .D(multiplexer_2_out), .Q(QB));  // open: Qn, preset, en, reset
  D_Flip_Flop d_ff_3 (.clk(not_4_out), .D(multiplexer_3_out), .Q(QC));  // open: Qn, preset, en, reset
  D_Flip_Flop d_ff_4 (.clk(not_4_out), .D(multiplexer_4_out), .Q(QD), .Qn(QDNOT));  // open: preset, en, reset
endmodule

module _74xx133 (
  input  A,
  input  B,
  input  C,
  input  D,
  input  E,
  input  F,
  input  G,
  input  H,
  input  I,
  input  J,
  input  K,
  input  L,
  input  M,
  input  Vcc,
  input  GND,
  output Y
);

  wire not_1_out, not_2_out, not_3_out, not_4_out, not_5_out, not_6_out, not_7_out, not_8_out, not_9_out,
       not_10_out, not_11_out, not_12_out, not_13_out, or_1_out, or_2_out, or_3_out;

  not not_1 (not_1_out, A);
  not not_2 (not_2_out, B);
  not not_3 (not_3_out, C);
  not not_4 (not_4_out, D);
  not not_5 (not_5_out, E);
  not not_6 (not_6_out, F);
  not not_7 (not_7_out, G);
  not not_8 (not_8_out, H);
  not not_9 (not_9_out, I);
  not not_10 (not_10_out, J);
  not not_11 (not_11_out, K);
  not not_12 (not_12_out, L);
  not not_13 (not_13_out, M);
  or or_1 (or_1_out, not_1_out, not_2_out, not_3_out, not_4_out, not_5_out);
  or or_2 (or_2_out, not_6_out, not_7_out, not_8_out, not_9_out, not_10_out);
  or or_3 (or_3_out, not_11_out, not_12_out, not_13_out);
  or or_4 (Y, or_1_out, or_2_out, or_3_out);
endmodule

module _74xx134 (
  input  A,
  input  B,
  input  C,
  input  D,
  input  E,
  input  F,
  input  G,
  input  H,
  input  I,
  input  J,
  input  K,
  input  L,
  input  OCNOT,
  input  Vcc,
  input  GND,
  output Y
);

  wire not_1_out, not_2_out, not_3_out, not_4_out, not_5_out, not_6_out, not_7_out, not_8_out, not_9_out,
       not_10_out, not_11_out, not_12_out, not_13_out, or_1_out, or_2_out, or_3_out, or_4_out;

  not not_1 (not_1_out, OCNOT);
  not not_2 (not_2_out, A);
  not not_3 (not_3_out, B);
  not not_4 (not_4_out, C);
  not not_5 (not_5_out, D);
  not not_6 (not_6_out, E);
  not not_7 (not_7_out, F);
  not not_8 (not_8_out, G);
  not not_9 (not_9_out, H);
  not not_10 (not_10_out, I);
  not not_11 (not_11_out, J);
  not not_12 (not_12_out, K);
  not not_13 (not_13_out, L);
  or or_1 (or_1_out, not_2_out, not_3_out, not_4_out, not_5_out, not_6_out);
  or or_2 (or_2_out, not_7_out, not_8_out, not_9_out, not_10_out, not_11_out);
  or or_3 (or_3_out, not_12_out, not_13_out);
  or or_4 (or_4_out, or_1_out, or_2_out, or_3_out);
  assign Y = not_1_out ? or_4_out : 1'bz;  // Controlled_Buffer controlled_buffer_1
endmodule

module _74xx150 (
  input  A,
  input  B,
  input  C,
  input  D,
  input  E0,
  input  E1,
  input  E2,
  input  E3,
  input  E4,
  input  E5,
  input  E6,
  input  E7,
  input  E8,
  input  E9,
  input  E10,
  input  E11,
  input  E12,
  input  E13,
  input  E14,
  input  E15,
  input  G,
  input  Vcc,
  input  GND,
  output Y
);

  wire and_1_out, and_2_out, and_3_out, and_4_out, and_5_out, and_6_out, and_7_out, and_8_out, and_9_out,
       and_10_out, and_11_out, and_12_out, and_13_out, and_14_out, and_15_out, and_16_out, not_1_out,
       not_2_out, not_3_out, not_4_out, not_5_out, not_6_out, not_7_out, not_8_out, not_9_out, not_10_out,
       not_11_out, not_12_out, not_13_out, not_14_out, not_15_out, not_16_out, not_17_out, not_18_out,
       not_19_out, not_20_out, or_1_out, or_2_out, or_3_out;

  not not_1 (not_1_out, E0);
  not not_2 (not_2_out, E1);
  not not_3 (not_3_out, E2);
  not not_4 (not_4_out, E3);
  not not_5 (not_5_out, E4);
  not not_6 (not_6_out, E5);
  not not_7 (not_7_out, E6);
  not not_8 (not_8_out, E7);
  not not_9 (not_9_out, E8);
  not not_10 (not_10_out, E9);
  not not_11 (not_11_out, E10);
  not not_12 (not_12_out, E11);
  not not_13 (not_13_out, E12);
  not not_14 (not_14_out, E13);
  not not_15 (not_15_out, E14);
  not not_16 (not_16_out, E15);
  not not_17 (not_17_out, A);
  not not_18 (not_18_out, B);
  not not_19 (not_19_out, C);
  not not_20 (not_20_out, D);
  and and_1 (and_1_out, A, not_18_out, C, B, not_14_out);
  and and_2 (and_2_out, not_17_out, B, C, B, not_15_out);
  and and_3 (and_3_out, A, B, C, B, not_16_out);
  and and_4 (and_4_out, A, B, not_19_out, D, not_12_out);
  and and_5 (and_5_out, not_17_out, not_18_out, C, B, not_13_out);
  and and_6 (and_6_out, not_17_out, not_18_out, not_19_out, D, not_9_out);
  and and_7 (and_7_out, A, not_18_out, not_19_out, D, not_10_out);
  and and_8 (and_8_out, not_17_out, B, not_19_out, D, not_11_out);
  and and_9 (and_9_out, A, not_18_out, C, not_6_out);
  and and_10 (and_10_out, not_17_out, B, C, not_20_out, not_7_out);
  and and_11 (and_11_out, A, B, C, not_20_out, not_8_out);
  and and_12 (and_12_out, not_17_out, B, not_19_out, not_20_out, not_3_out);
  and and_13 (and_13_out, A, B, not_19_out, not_20_out, not_4_out);
  and and_14 (and_14_out, not_17_out, not_18_out, C, not_20_out, not_5_out);
  or or_1 (or_1_out, and_8_out, and_4_out, and_5_out, and_1_out, and_2_out);
  and and_15 (and_15_out, not_17_out, not_18_out, not_19_out, not_20_out, not_1_out);
  and and_16 (and_16_out, A, not_18_out, not_19_out, not_20_out, not_2_out);
  or or_2 (or_2_out, and_9_out, and_10_out, and_11_out, and_6_out, and_7_out);
  or or_3 (or_3_out, and_15_out, and_16_out, and_12_out, and_13_out, and_14_out);
  or or_4 (Y, or_3_out, or_2_out, or_1_out, and_3_out, G);
endmodule

module _74xx165 (
  input  A,
  input  B,
  input  C,
  input  D,
  input  E,
  input  F,
  input  G,
  input  H,
  input  SH_LDNOT,
  input  CLK,
  input  CLK_INH,
  input  SER,
  input  Vcc,
  input  GND,
  output QH,
  output QHNOT
);

  wire and_1_out, and_2_out, and_3_out, and_4_out, and_5_out, and_6_out, and_7_out, and_8_out, and_9_out,
       and_10_out, and_11_out, and_12_out, and_13_out, and_14_out, and_15_out, and_16_out, d_ff_1_q,
       d_ff_2_q, d_ff_3_q, d_ff_4_q, d_ff_5_q, d_ff_6_q, d_ff_7_q, not_1_out, not_2_out, not_3_out,
       not_4_out, not_5_out, not_6_out, not_7_out, not_8_out, not_9_out, or_1_out;

  not not_1 (not_1_out, SH_LDNOT);
  not not_2 (not_2_out, A);
  not not_3 (not_3_out, B);
  not not_4 (not_4_out, C);
  not not_5 (not_5_out, D);
  or or_1 (or_1_out, CLK, CLK_INH);
  not not_6 (not_6_out, E);
  not not_7 (not_7_out, F);
  not not_8 (not_8_out, G);
  not not_9 (not_9_out, H);
  and and_1 (and_1_out, not_1_out, A);
  and and_2 (and_2_out, not_1_out, not_2_out);
  and and_3 (and_3_out, not_1_out, B);
  and and_4 (and_4_out, not_1_out, not_3_out);
  and and_5 (and_5_out, not_1_out, C);
  and and_6 (and_6_out, not_1_out, not_4_out);
  and and_7 (and_7_out, not_1_out, D);
  and and_8 (and_8_out, not_1_out, not_5_out);
  and and_9 (and_9_out, not_1_out, E);
  and and_10 (and_10_out, not_1_out, not_6_out);
  and and_11 (and_11_out, not_1_out, F);
  and and_12 (and_12_out, not_1_out, not_7_out);
  and and_13 (and_13_out, not_1_out, G);
  and and_14 (and_14_out, not_1_out, not_8_out);
  and and_15 (and_15_out, not_1_out, H);
  and and_16 (and_16_out, not_1_out, not_9_out);
  D_Flip_Flop d_ff_1 (.clk(or_1_out), .D(SER), .Q(d_ff_1_q), .preset(and_1_out), .reset(and_2_out));  // open: Qn, en
  D_Flip_Flop d_ff_2 (
    .clk(or_1_out), .D(d_ff_1_q), .Q(d_ff_2_q), .preset(and_3_out), .reset(and_4_out));  // open: Qn, en
  D_Flip_Flop d_ff_3 (
    .clk(or_1_out), .D(d_ff_2_q), .Q(d_ff_3_q), .preset(and_5_out), .reset(and_6_out));  // open: Qn, en
  D_Flip_Flop d_ff_4 (
    .clk(or_1_out), .D(d_ff_3_q), .Q(d_ff_4_q), .preset(and_7_out), .reset(and_8_out));  // open: Qn, en
  D_Flip_Flop d_ff_5 (
    .clk(or_1_out), .D(d_ff_4_q), .Q(d_ff_5_q), .preset(and_9_out), .reset(and_10_out));  // open: Qn, en
  D_Flip_Flop d_ff_6 (
    .clk(or_1_out), .D(d_ff_5_q), .Q(d_ff_6_q), .preset(and_11_out), .reset(and_12_out));  // open: Qn, en
  D_Flip_Flop d_ff_7 (
    .clk(or_1_out), .D(d_ff_6_q), .Q(d_ff_7_q), .preset(and_13_out), .reset(and_14_out));  // open: Qn, en
  D_Flip_Flop d_ff_8 (
    .clk(or_1_out), .D(d_ff_7_q), .Q(QH), .Qn(QHNOT), .preset(and_15_out), .reset(and_16_out));  // open: en

  // Notes on the sheet:
  //   TO SHIFT, SH/LD HIGH
endmodule

module _74xx180 (
  input  A,
  input  B,
  input  C,
  input  D,
  input  E,
  input  F,
  input  G,
  input  H,
  input  EVEN,
  input  ODD,
  input  Vcc,
  input  GND,
  output SUMEVEN,
  output SUMODD
);

  wire and_1_out, and_2_out, and_3_out, and_4_out, not_1_out, not_2_out, not_3_out, not_4_out, not_5_out,
       xor_1_out, xor_2_out, xor_3_out, xor_4_out, xor_5_out, xor_6_out, xor_7_out;

  xor xor_1 (xor_1_out, A, B);
  xor xor_2 (xor_2_out, xor_1_out, C);
  xor xor_3 (xor_3_out, xor_2_out, D);
  xor xor_4 (xor_4_out, xor_3_out, E);
  xor xor_5 (xor_5_out, xor_4_out, F);
  xor xor_6 (xor_6_out, xor_5_out, G);
  xor xor_7 (xor_7_out, xor_6_out, H);
  not not_1 (not_1_out, EVEN);
  not not_2 (not_2_out, ODD);
  not not_3 (not_3_out, xor_7_out);
  not not_4 (not_4_out, EVEN);
  not not_5 (not_5_out, ODD);
  and and_1 (and_1_out, xor_7_out, not_1_out);
  and and_2 (and_2_out, not_2_out, not_3_out);
  and and_3 (and_3_out, not_3_out, not_4_out);
  and and_4 (and_4_out, xor_7_out, not_5_out);
  or or_1 (SUMEVEN, and_1_out, and_2_out);
  or or_2 (SUMODD, and_3_out, and_4_out);
endmodule
